// Logisim project CU.circ as structural Verilog: 2 circuits, main circuit CU
module CU (
  input  [7:0] in_1,
  output [3:0] Address,
  output Stop,
  output out_4,
  output Add,
  output Sub,
  output Beq,
  output Bnq,
  output Ld1,
  output Ld2,
  output Str1,
  output Str2,
  output Prt,
  output Inp
);

  Decoder #(.select(4), .enable("false")) decoder_1 (
    .out0(Stop), .out1(out_4), .out2(Add), .out3(Sub), .out4(Beq), .out5(Bnq), .out6(Ld1), .out7(Ld2),
    .out8(Str1), .out9(Str2), .out10(Prt), .out11(Inp), .sel(in_1[7:4]));  // open: out12, out13, out14, out15

  assign Address = in_1[3:0];
endmodule

module DataRegisters (
  input  Clk,
  input  Rw,
  input  Which,
  input  [7:0] in_4,
  output [7:0] DataOutput,
  output Eq
);

  wire and_1_out, and_2_out, xnor_1_out, xnor_2_out, xnor_3_out, xnor_4_out, xnor_5_out, xnor_6_out,
       xnor_7_out, xnor_8_out;
  wire [7:0] byte_storage_compact_1_out_4, byte_storage_compact_2_out_4;

  xnor xnor_1 (xnor_1_out, byte_storage_compact_2_out_4[7], byte_storage_compact_1_out_4[7]);
  xnor xnor_2 (xnor_2_out, byte_storage_compact_2_out_4[6], byte_storage_compact_1_out_4[6]);
  and and_1 (and_1_out, Rw, ~Which);  // AND_Gate
  and and_2 (and_2_out, Rw, Which);
  xnor xnor_3 (xnor_3_out, byte_storage_compact_2_out_4[4], byte_storage_compact_1_out_4[4]);
  xnor xnor_4 (xnor_4_out, byte_storage_compact_2_out_4[5], byte_storage_compact_1_out_4[5]);
  byte_storage_compact byte_storage_compact_1 (
    .in_3(in_4), .out_4(byte_storage_compact_1_out_4), .EnableWrite(and_1_out), .Clock(Clk));
  byte_storage_compact byte_storage_compact_2 (
    .in_3(in_4), .out_4(byte_storage_compact_2_out_4), .EnableWrite(and_2_out), .Clock(Clk));
  xnor xnor_5 (xnor_5_out, byte_storage_compact_2_out_4[3], byte_storage_compact_1_out_4[3]);
  Multiplexer #(.width(8), .enable("false")) multiplexer_1 (
    .in0(byte_storage_compact_1_out_4), .in1(byte_storage_compact_2_out_4), .out(DataOutput), .sel(Which));
  xnor xnor_6 (xnor_6_out, byte_storage_compact_2_out_4[1], byte_storage_compact_1_out_4[1]);
  xnor xnor_7 (xnor_7_out, byte_storage_compact_2_out_4[2], byte_storage_compact_1_out_4[2]);
  xnor xnor_8 (xnor_8_out, byte_storage_compact_2_out_4[0], byte_storage_compact_1_out_4[0]);
  and and_3 (Eq, xnor_8_out, xnor_6_out, xnor_7_out, xnor_5_out, xnor_3_out, xnor_4_out, xnor_2_out, xnor_1_out);
endmodule
